# Fritzing sketch wiretapping (saved by Fritzing 0.9.3b)
breadboards: 1

parts:
  Status_from_AC = CP2102 USB UART Breakout
  X1 = USB Connectors [package=usb-a-s-nosilk]
  X2 = USB Connectors [package=usb-a-s-nosilk]
  Commands_from_WiFi_Module = CP2102 USB UART Breakout

nets:
  GND: Status_from_AC.GND, X1.GND, X2.GND, Commands_from_WiFi_Module.GND
  N1: Status_from_AC.RXD, X1.D+, X2.D+
  N2: X1.D-, X2.D-, Commands_from_WiFi_Module.RXD
  N3: X1.VBUS, X2.VBUS

custom parts:
  CP2102 USB UART Breakout: CP2102 Usb Uart Breakout Board with Battery
