# Fritzing sketch haier (saved by Fritzing 0.9.3b)

parts:
  WeMos_D1_Mini1 = WeMos D1 Mini
  X1 = USB Connectors [package=usb-a-s-silk-female]

nets:
  N1: WeMos_D1_Mini1.5V, X1.VBUS
  N2: WeMos_D1_Mini1.G, X1.GND
  N3: WeMos_D1_Mini1.RX, X1.D+
  N4: WeMos_D1_Mini1.TX, X1.D-
